# Fritzing sketch Safety Printer (saved by Fritzing 0.9.6b)
perfboards: 1

parts:
  part = Arduino Nano (Rev3.0)
  R4 = Resistor [tolerance=±5% power=0.25 resistance=470 package=THT]
  R5 = Resistor [tolerance=±5% power=0.25 resistance=1000 package=THT]
  Flame_2 = JST-03JQ-BT [part_number=JST-JQ-BT package=THT]
  LED2 = LEDs [package=led10mm]
  S2 = Pushbutton [package="[SMD]"]
  R3 = Resistor [tolerance=±5% power=0.25 resistance=470 package=THT]
  Flame_1 = JST-03JQ-BT [part_number=JST-JQ-BT package=THT]
  Interlock_Relay = JST-03JQ-BT [part_number=JST-JQ-BT package=THT]
  R2 = Resistor [tolerance=±5% power=0.25 resistance=1000 package=THT]
  LED1 = LEDs [package=led10mm]
  R1 = Resistor [tolerance=±5% power=0.25 resistance=1000 package=THT]
  Smoke_Power = Header 2 [package=jst-2-smd]
  Smoke_Signal = Header 2 [package=jst-2-smd]
  Emergency_Button = Screw terminal - 2 pins [package=THT]
  Step_Up_Buck_Converter = RioRand LM2596

nets:
  N1: part.GND, R4.Pin_1, R5.Pin_1, Flame_2.pin2, R3.Pin_1, Flame_1.pin2, Interlock_Relay.pin2, R2.Pin_1, R1.Pin_1
  N2: part.D5, R2.Pin_0, Emergency_Button.pin2
  N3: part.D6, Interlock_Relay.pin3
  N4: part.D7, R1.Pin_0, Smoke_Signal.2
  N5: part.D8, Flame_2.pin1
  N6: part.D9, Flame_1.pin1
  N7: part.D10, LED2.A
  N8: part.D11/MOSI, S2.Pin_3
  N9: part.D12/MISO, LED1.A
  N10: part.5V, Flame_2.pin3, Flame_1.pin3, Interlock_Relay.pin1, Smoke_Signal.1, Emergency_Button.pin1, Step_Up_Buck_Converter.Pin_1
  N11: R4.Pin_0, LED1.C
  N12: R5.Pin_0, S2.Pin_1, S2.Pin_2
  N13: LED2.C, R3.Pin_0
  N14: Smoke_Power.2, Step_Up_Buck_Converter.Pin_4
  N15: Smoke_Power.1, Step_Up_Buck_Converter.Pin_3
